// Digital circuit 8BitShift.dig as structural Verilog
module _8BitShift (
  input  clk,
  input  [7:0] in,
  output [7:0] o1,
  output [7:0] o2,
  output [7:0] o3,
  output [7:0] o4,
  output [7:0] o5,
  output [7:0] o6,
  output [7:0] o7,
  output [7:0] o8
);

  D_FF #(.Bits(8)) d_ff_1 (.D(in), .C(clk), .Q(o1));  // open: nQ
  D_FF #(.Bits(8)) d_ff_2 (.D(o1), .C(clk), .Q(o2));  // open: nQ
  D_FF #(.Bits(8)) d_ff_3 (.D(o2), .C(clk), .Q(o3));  // open: nQ
  D_FF #(.Bits(8)) d_ff_4 (.D(o3), .C(clk), .Q(o4));  // open: nQ
  D_FF #(.Bits(8)) d_ff_5 (.D(o4), .C(clk), .Q(o5));  // open: nQ
  D_FF #(.Bits(8)) d_ff_6 (.D(o5), .C(clk), .Q(o6));  // open: nQ
  D_FF #(.Bits(8)) d_ff_7 (.D(o6), .C(clk), .Q(o7));  // open: nQ
  D_FF #(.Bits(8)) d_ff_8 (.D(o7), .C(clk), .Q(o8));  // open: nQ
endmodule
