// Digital circuit main.dig as structural Verilog
module main (
  input  clk,
  input  in_2,
  input  in_3,
  output out_4
);

  wire demultiplexer_1_out_1, multiplexer_1_out, not_1_out;

  Multiplexer multiplexer_1 (.sel(clk), .in_0(in_2), .in_1(in_3), .out(multiplexer_1_out));
  // Not not_1 has open pins: in=open, out=not_1_out
  Demultiplexer demultiplexer_1 (.sel(not_1_out), .in(multiplexer_1_out), .out_0(out_4), .out_1(demultiplexer_1_out_1));
endmodule
